# Fritzing sketch Type4-esp-12F-v132-BIGSIZE--SMD1206 (saved by Fritzing 0.9.3b)
circuit board: 8cm x 2.5cm
breadboards: 1

parts:
  ESP-12F = ESP8266 WiFi Module [part_number=ESP8266]
  BC547 = PNP-Transistor [package="TO92 [THT]"]
  DIODE = Rectifier Diode [part_number=1N4001 package="300 mil [THT]"]
  TX/RX = male pin header, 2 pins [form="♂ (male)"]
  FAN1 = Header 2 [package=jst-2-pth-kit]
  FAN2 = Header 2 [package=jst-2-pth-kit]
  AMS1117 = Voltage Regulator -- 3.3 V -- LM1117
  +DHT- = Header 3 [package=jst-3-pth]
  470Ω = Resistor [tolerance=±5% resistance=470 package=THT]
  4_7kΩ = Resistor [tolerance=±5% resistance=4.7k package=THT]
  Oled = Grove OLED 128x96
  4_7kΩ_2 = Resistor [tolerance=±5% resistance=4.7k package=THT]
  10kΩ = Resistor [tolerance=±5% resistance=10k package=THT]
  4_7kΩ_3 = Resistor [tolerance=±5% resistance=4.7k package=THT]
  OLED_BTN = female pin header, 2 pins [form="♀ (female)"]
  RESET = SWITCH-MOMENTARY-2 [package=tactile-switch-1101ne]
  FLASH = SWITCH-MOMENTARY-2 [package=tactile-switch-1101ne]
  PWR = Header 3 [package=jst-3-pth]
  10kΩ1 = Resistor [tolerance=±5% resistance=10k package=THT]

nets:
  N1: ESP-12F.RXD, TX/RX.pin1
  VCC: ESP-12F.VCC, AMS1117.OUT, Oled.VCC, 4_7kΩ_2.Pin_0, 10kΩ.Pin_0, 4_7kΩ_3.Pin_0, 10kΩ1.Pin_1
  N2: ESP-12F.GPIO_0, FLASH.1
  N3: ESP-12F.GPIO_2, 4_7kΩ_2.Pin_1
  N4: ESP-12F.EN, 10kΩ1.Pin_0
  GND: ESP-12F.GND, BC547.C, AMS1117.GND, +DHT-.3, 4_7kΩ.Pin_0, Oled.GND, OLED_BTN.pin1, RESET.2, FLASH.2, PWR.1
  N5: ESP-12F.TXD, TX/RX.pin2
  N6: ESP-12F.GPIO_15, 4_7kΩ.Pin_1
  N7: ESP-12F.GPIO_4, Oled.SDA
  N8: ESP-12F.GPIO_5, Oled.SCL
  N9: ESP-12F.GPIO_16, 470Ω.Pin_1
  N10: ESP-12F.GPIO_14, 10kΩ.Pin_1, OLED_BTN.pin2
  N11: ESP-12F.GPIO_13, +DHT-.2
  N12: ESP-12F.REST, 4_7kΩ_3.Pin_1, RESET.1
  N13: BC547.E, DIODE.anode, FAN1.1, FAN2.1, PWR.3
  N14: BC547.B, 470Ω.Pin_0
  N15: DIODE.cathode, FAN1.2, FAN2.2, AMS1117.IN, +DHT-.1, PWR.2

notes:
  Prog
  Reset
  GND OUT  IN
  -   + DATA

custom parts:
  ESP8266 WiFi Module: Generic WiFi Module based on the ESP8266 with onboard PCB antenna and UART communications
  Voltage Regulator -- 3.3 V -- LM1117: LM1117-3.3 Voltage regulator, 3.3 V output. Note that the pinout order is not the same as LM7805 or LM7833.
